# Fritzing sketch esp8266_schematic (saved by Fritzing 1.0.0rc)
breadboards: 1

parts:
  SP1 = SPEAKER [package=pcb_mount_speaker]
  U1 = ESP8266 ESP-01 Upgraded WiFi Module [part_number=ESP8266]

nets:
  N1: SP1.+, U1.GND
  N2: SP1.-, U1.RXD
  N3: U1.VCC, U1.CH_PD

custom parts:
  ESP8266 ESP-01 Upgraded WiFi Module: Upgraded Version ESP-01,all Flash are upgraded to 1M byte.Also support Cloud service remote transmission.
